// Logisim project Question1.circ as structural Verilog
module main (
  input  in_1,
  input  in_2,
  input  in_3,
  input  in_4
);

  wire q1_1_out1, q1_1_out2;

  Q1 q1_1 (.a(in_1), .b(in_2), .c(in_3), .d(in_4), .out1(q1_1_out1), .out2(q1_1_out2));
  LED led_1 (.in(q1_1_out1));
  LED led_2 (.in(q1_1_out2));
endmodule

// VHDL entity Q1, as the project stores it:
--------------------------------------------------------------------------------
-- Project :
-- File    :
-- Autor   :
-- Date    :
--
--------------------------------------------------------------------------------
-- Description :
--
--------------------------------------------------------------------------------


-- library and package
library ieee;
use ieee.std_logic_1164.all;
use ieee.std_logic_arith.all;
use ieee.std_logic_unsigned.all;

-- entity
entity Q1 is
    port(
          a, b, c, d: in std_logic;    -- four 1-bit input signals
          out1, out2: out std_logic    -- two 1-bit output signals
        );
end entity Q1;

-- architecture
architecture bhv of Q1 is
begin
    out1 <= a and b and c and d;
    out2 <= a or b or c or d;
end architecture bhv;
