// Logisim project Question2.circ as structural Verilog
module main (
  input  in_1,
  input  in_2,
  input  in_3,
  input  in_4,
  input  in_5,
  input  in_6,
  input  in_7,
  input  in_8,
  input  [2:0] in_9
);

  wire q2_1_data;

  Q2 q2_1 (.a(in_1), .b(in_2), .c(in_3), .d(in_4), .e(in_5), .f(in_6), .g(in_7), .h(in_8), .ch(in_9), .data(q2_1_data));
  LED led_1 (.in(q2_1_data));
endmodule

// VHDL entity Q2, as the project stores it:
--------------------------------------------------------------------------------
-- Project :
-- File    :
-- Autor   :
-- Date    :
-- 
--------------------------------------------------------------------------------
-- Description :
--
--------------------------------------------------------------------------------


-- library and package
library ieee;
use ieee.std_logic_1164.all;
use ieee.std_logic_arith.all;
use ieee.std_logic_unsigned.all;

-- entity
entity Q2 is
    port(
          a, b, c, d, e, f, g, h: in std_logic;    -- 8 input signals
          ch: in std_logic_vector(2 downto 0);    -- 3-bit selector
          data: out std_logic    -- output signal
        );
end entity Q2;

-- architecture
architecture bhv of Q2 is
begin
    process(a, b, c, d, e, f, g, h, ch)
    begin
        case ch is
            when "000" => data <= a;    -- if ch = 0, choose input a
            when "001" => data <= b;    -- if ch = 1, choose input b
            when "010" => data <= c;    -- if ch = 2, choose input c
            when "011" => data <= d;    -- if ch = 3, choose input d
            when "100" => data <= e;    -- if ch = 4, choose input e
            when "101" => data <= f;    -- if ch = 5, choose input f
            when "110" => data <= g;    -- if ch = 6, choose input g
            when "111" => data <= h;    -- if ch = 7, choose input h
            when others => data <= '0';
        end case;
    end process;
end architecture bhv;
